# Fritzing sketch many-pins-diodes (saved by Fritzing 0.9.2b)
breadboards: 1

parts:
  Dudu = Arduino Nano (Rev3.0)
  LED1 = LED - 5mm [color="Red (633nm)" package="5 mm [THT]"]
  Diode = PNP-Transistor [package="TO92 [THT]"]
  Diode_2 = PNP-Transistor [package="TO92 [THT]"]
  Diode_3 = PNP-Transistor [package="TO92 [THT]"]
  Diode_4 = PNP-Transistor [package="TO92 [THT]"]
  Letter_2 = LED - 3mm [color="Blue (505nm)" package="3 mm [THT]"]

nets:
  N1: Dudu.GND, LED1.cathode, Letter_2.cathode
  N2: Dudu.D2, Diode.E
  N3: Dudu.D3, Diode_2.E
  N4: Dudu.5V, Diode.C
  N5: Dudu.D13/SCK, Diode_3.C, Diode_4.C
  N6: LED1.anode, Diode_3.B
  N7: Diode.B, Diode_3.E
  N8: Diode_2.B, Diode_4.E
  N9: Diode_4.B, Letter_2.anode
